# Fritzing sketch digital-save Frtizing (saved by Fritzing 0.9.3b)
breadboards: 1

parts:
  KEYPAD1 = Membrane Matrix Keypad
  Part1 = LCD1602-I2C
  LED1 = smd LED [color="Green (555nm)" package="0805 [SMD]"]
  LED2 = smd LED [color="Red (633nm)" package="0805 [SMD]"]
  Part2 = Arduino Mega 2560 (Rev3)
  GSM_SIM_GPSR_SMS_SIM900_SIM1 = SIM800L [package=THT]
  J1 = Piezo Speaker
  KY-1 = Keyes Relay [package=THT]
  L1 = Solenoid
  KY-2 = Keyes Relay [package=THT]
  R1 = Resistor [tolerance=±5% resistance=220 package=THT]
  R2 = Resistor [tolerance=±5% resistance=220 package=THT]

nets:
  N1: KEYPAD1.1, Part2.D8_PWM
  N2: KEYPAD1.2, Part2.D7_PWM
  N3: KEYPAD1.3, Part2.D6_PWM
  N4: KEYPAD1.4, Part2.D5_PWM
  N5: KEYPAD1.5, Part2.D4_PWM
  N6: KEYPAD1.6, Part2.D3_PWM
  N7: KEYPAD1.7, Part2.D2_PWM
  N8: Part1.SDA, Part2.D20/SDA
  N9: Part1.SCL, Part2.D21/SCL
  N10: LED1.cathode, LED2.cathode
  N11: LED1.anode, R2.Pin_1
  N12: LED2.anode, R1.Pin_1
  N13: Part2.D19/RX1, GSM_SIM_GPSR_SMS_SIM900_SIM1.SIM_TXD
  N14: Part2.D18/TX1, GSM_SIM_GPSR_SMS_SIM900_SIM1.SIM_RXD
  N15: Part2.D10_PWM, KY-2.signal
  N16: Part2.D9_PWM, KY-1.signal
  N17: Part2.D22, R2.Pin_0
  N18: Part2.D23, R1.Pin_0
  N19: J1.pin2, KY-2.NO
  N20: KY-1.NO, L1.pin2

custom parts:
  Membrane Matrix Keypad: Membrane Matrix 3x4 Keypad
  LCD1602-I2C: A standard character display, usually with 2x16 characters. Comes in many colors with LCM1602 IIC attached.
  Keyes Relay: The Keyes 5V relay module is suitable for SCM development, home appliance control. It uses a 5V~12V TIL control signal which can control DC / AC signal.
